# Fritzing sketch p2.sketch (saved by Fritzing 1.0.4)
breadboards: 1

parts:
  R1 = Resistor [tolerance=±5% power=0.25W resistance=220 package=THT]
  S1 = Pushbutton [package="[THT]"]  # not connected
  R2 = 6mm Trimmer Potentiometer [maximum_resistance=10kΩ knob_status=50% power=0.5W package=THT]  # not connected
  Part1 = Thumb Joystick
  R3 = Rotary Potentiometer (Small) [maximum_resistance=10kΩ knob_status=50% power=0.5W package=THT]  # not connected
  C1 = Tantalum Capacitor [capacitance=1μF voltage=35V package="100 mil [THT, tantalum]"]
  Mod2 = ESP32-TTGO-T-DISPLAY
  VCC1 = Battery [internal_resistance=0.1Ω]

nets:
  N1: R1.Pin_0, C1.+
  N2: R1.Pin_1, Mod2.15
  N3: Part1.GND, VCC1.-
  N4: Part1.SEL, Mod2.33
  N5: Part1.HORZ, Mod2.39
  N6: Part1.VERT, Mod2.32
  N7: C1.-, Mod2.G-1, Mod2.G-2, Mod2.G-10, Mod2.G-11, Mod2.G-14

custom parts:
  ESP32-TTGO-T-DISPLAY: LILYGO TTGO T-Display GD32VF103CBT6 Main Chip ST7789 1.14 Inch IPS 240x135 Resolution Minimalist Development Board.

// code stored in the sketch: Untitled.ino
/*
  Serial Joystick
 Takes in X,Y,Z serial input from a joystick
 */

import processing.serial.*;

Serial myPort;  // Create object from Serial class
String val;      // Data received from the serial port

int canvasSize = 500;
int analogMax = 4095;

void setup()
{
  size(500, 500);
  printArray(Serial.list());
  String portName = Serial.list()[3];
  println(portName);
  myPort = new Serial(this, portName, 9600); // ensure baudrate is consistent with arduino sketch
}

void draw()
{
  if ( myPort.available() > 0) {  // If data is available,
    val = myPort.readStringUntil('\n');         // read it and store it in val
  }
  val = trim(val);
  if ( val != null ) {
    background(255);
    println(val);
    int[] xyz = int(split(val, ','));

    // use if statement to check serial input length to prevent ArrayIndexOutOfBounds errors
    if (xyz.length == 3) {
      int x = xyz[0];
      int y = xyz[1];
      int z = xyz[2];

      float circleX = map(x, 0, analogMax, 0, canvasSize);
      float circleY = map(y, 0, analogMax, 0, canvasSize);
      int fillColor = (z == 1 ? 0 : 255);

      fill(fillColor);
      circle(circleX, circleY, 25);
    }
  }
}
